// Logisim project schematomasik.circ as structural Verilog: 1 circuit, main circuit main
module main (
  input  A,
  input  B,
  input  C,
  input  D
);

  wire and_1_out, and_2_out, and_3_out, and_4_out, and_5_out, and_6_out, and_7_out, and_8_out, and_9_out,
       and_10_out, and_11_out, and_12_out, and_13_out, and_14_out, and_15_out, and_16_out, and_17_out,
       and_18_out, and_19_out, and_20_out, and_21_out, and_22_out, and_23_out, and_24_out, and_25_out,
       and_26_out, and_27_out, and_28_out, and_29_out, and_30_out, and_31_out, and_32_out, and_33_out,
       and_34_out, and_35_out, not_1_out, not_2_out, not_3_out, not_4_out, not_5_out, not_6_out, not_7_out,
       not_8_out, not_9_out, not_10_out, not_11_out, not_12_out, not_13_out, not_14_out, not_15_out,
       not_16_out, not_17_out, not_18_out, not_19_out, not_20_out, not_21_out, not_22_out, not_23_out,
       not_24_out, not_25_out, not_26_out, not_27_out, not_29_out, not_30_out, not_31_out, not_32_out,
       not_33_out, not_34_out, not_35_out, not_36_out, not_37_out, not_38_out, not_39_out, not_40_out,
       not_41_out, not_42_out, not_43_out, not_44_out, or_1_out, or_2_out, or_3_out, or_4_out, or_5_out,
       or_6_out, or_7_out, or_8_out;

  not not_1 (not_1_out, A);
  not not_2 (not_2_out, A);
  not not_3 (not_3_out, D);
  not not_4 (not_4_out, D);
  not not_5 (not_5_out, A);
  not not_6 (not_6_out, C);
  not not_7 (not_7_out, A);
  not not_8 (not_8_out, D);
  not not_9 (not_9_out, A);
  not not_10 (not_10_out, A);
  not not_11 (not_11_out, C);
  not not_12 (not_12_out, C);
  not not_13 (not_13_out, D);
  not not_14 (not_14_out, A);
  not not_15 (not_15_out, A);
  not not_16 (not_16_out, A);
  not not_17 (not_17_out, D);
  not not_18 (not_18_out, C);
  not not_19 (not_19_out, C);
  not not_20 (not_20_out, A);
  not not_21 (not_21_out, A);
  not not_22 (not_22_out, C);
  not not_23 (not_23_out, A);
  not not_24 (not_24_out, D);
  not not_25 (not_25_out, C);
  not not_26 (not_26_out, D);
  not not_27 (not_27_out, A);
  not not_28 (not_27_out, C);
  not not_29 (not_29_out, D);
  not not_30 (not_30_out, D);
  not not_31 (not_31_out, A);
  not not_32 (not_32_out, A);
  not not_33 (not_33_out, C);
  not not_34 (not_34_out, A);
  not not_35 (not_35_out, C);
  not not_36 (not_36_out, D);
  not not_37 (not_37_out, A);
  not not_38 (not_38_out, A);
  not not_39 (not_39_out, A);
  not not_40 (not_40_out, D);
  not not_41 (not_41_out, A);
  not not_42 (not_42_out, D);
  not not_43 (not_43_out, C);
  not not_44 (not_44_out, D);
  and and_1 (and_1_out, not_1_out, C);
  and and_2 (and_2_out, C, A);
  and and_3 (and_3_out, not_2_out, not_3_out);
  and and_4 (and_4_out, not_4_out, A);
  and and_5 (and_5_out, A, not_5_out, not_6_out);
  or or_1 (or_1_out, and_5_out, and_6_out);
  and and_6 (and_6_out, not_7_out, A, D);
  and and_7 (and_7_out, A, not_8_out);
  and and_8 (and_8_out, A, not_9_out);
  and and_9 (and_9_out, A, C);
  and and_10 (and_10_out, not_10_out, A, not_11_out);
  and and_11 (and_11_out, not_12_out, not_13_out);
  and and_12 (and_12_out, not_14_out, not_15_out);
  and and_13 (and_13_out, not_16_out, not_17_out, not_18_out);
  and and_14 (and_14_out, A, not_19_out, D);
  and and_15 (and_15_out, D, C, A);
  and and_16 (and_16_out, not_20_out, D, C);
  and and_17 (and_17_out, not_21_out, A);
  and and_18 (and_18_out, D, A, not_22_out);
  and and_19 (and_19_out, C, A);
  and and_20 (and_20_out, not_23_out, not_24_out);
  buf and_21 (and_21_out, not_25_out);  // AND_Gate
  and and_22 (and_22_out, A, not_26_out);
  and and_23 (and_23_out, A, C);
  and and_24 (and_24_out, not_27_out, not_27_out, not_29_out);
  and and_25 (and_25_out, A, not_30_out);
  and and_26 (and_26_out, A, not_31_out);
  and and_27 (and_27_out, A, not_32_out);
  and and_28 (and_28_out, D, not_33_out);
  and and_29 (and_29_out, A, not_34_out);
  and and_30 (and_30_out, not_35_out, not_36_out, not_37_out);
  and and_31 (and_31_out, not_38_out, not_39_out, not_40_out);
  buf and_32 (and_32_out, not_41_out);  // AND_Gate
  and and_33 (and_33_out, A, D);
  and and_34 (and_34_out, A, not_42_out);
  and and_35 (and_35_out, A, not_44_out, not_44_out, not_43_out);
  or or_2 (or_2_out, and_1_out, and_2_out, and_3_out, and_4_out, or_1_out);
  or or_3 (or_3_out, and_7_out, and_8_out, and_9_out, and_10_out, and_11_out);
  or or_4 (or_4_out, and_12_out, and_13_out, and_14_out, and_15_out, and_16_out);
  or or_5 (or_5_out, and_17_out, and_18_out, and_19_out, and_20_out, and_21_out);
  or or_6 (or_6_out, and_22_out, and_23_out, and_24_out, and_25_out);
  or or_7 (or_7_out, and_26_out, and_27_out, and_28_out, and_29_out, and_30_out);
  or or_8 (or_8_out, and_31_out, and_32_out, and_33_out, and_34_out, and_35_out);
  _7_Segment_Display u_7_segment_display_1 (
    .g(or_5_out), .f(or_3_out), .a(or_2_out), .b(or_4_out), .e(or_6_out), .d(or_8_out), .c(or_7_out));  // open: dp

  assign B = A;

  // Notes on the sheet:
  //   Y3
  //   Y1
  //   Y2
  //   Y4
  //   Y5
  //   Y7
  //   Y6
endmodule
